# Fritzing sketch Heading Video Wiring Diagram (saved by Fritzing 0.9.9b)

parts:
  Part1 = Arduino Mega 2560 (Rev3)
  Driver1 = 28BYJ-48 Driver Module [part_number=ULN2003 package=THT]
  SM1 = 28BYJ-48 Stepper Motor [part_number=28BYJ-48]
  Driver2 = 28BYJ-48 Driver Module [part_number=ULN2003 package=THT]
  SM2 = 28BYJ-48 Stepper Motor [part_number=28BYJ-48]
  U2 = A3144 Hall Effect Sensor. [package="UA [THT]"]
  U3 = A3144 Hall Effect Sensor. [package="UA [THT]"]

nets:
  N1: Part1.D17_PWM/RX2, Driver2.IN4
  N2: Part1.D16_PWM/TX2, Driver2.IN3
  N3: Part1.D15/RX3, Driver2.IN2
  N4: Part1.D14/TX3, Driver2.IN1
  N5: Part1.D13_PWM, U2.Out
  N6: Part1.D12_PWM, Driver1.IN4
  N7: Part1.D11_PWM, Driver1.IN3
  N8: Part1.D10_PWM, Driver1.IN2
  N9: Part1.D9_PWM, Driver1.IN1
  N10: Part1.D8_PWM, U3.Out
  N11: Part1.5V, Driver1.Vmotor, Driver2.Vmotor, U2.+Vsupply, U3.+Vsupply
  GND: Part1.GND, Driver1.GND, Driver2.GND, U2.GND, U3.GND
  N12: Driver1.blue-pin, SM1.blue-pin
  N13: Driver1.pink-pin, SM1.pink-pin
  N14: Driver1.yellow-pin, SM1.yellow-pin
  N15: Driver1.orange-pin, SM1.orange-pin
  N16: Driver1.red-pin, SM1.red-pin
  N17: Driver2.blue-pin, SM2.blue-pin
  N18: Driver2.pink-pin, SM2.pink-pin
  N19: Driver2.yellow-pin, SM2.yellow-pin
  N20: Driver2.orange-pin, SM2.orange-pin
  N21: Driver2.red-pin, SM2.red-pin

custom parts:
  28BYJ-48 Driver Module: ULN2003 Driver Module for the 28BYJ-48 Unipolar Stepper Motor LED A - Blue wire - Bottom coil left LED B - Pink wire - Top coil left LED C - Yellow wire - Bottom coil right LED D - Orange wire - Top coil right Common rail - red Connector pins: blue - pink - yellow - orange - red Control pins - IN1 to IN4 Power pins - GND & Vmotor (5-12V) On/Off jumper (if removed, power to motor is cut).
  28BYJ-48 Stepper Motor: Unipolar Stepper Motor 28BYJ-48 Top coil - pink & orange Bottom coil - blue & yellow Common rail - red Connector pins: blue - pink - yellow - orange - red
  A3144 Hall Effect Sensor.: Allegro A3144 hall effect switch for high temperature operation.
