# Fritzing sketch Wiring Diagram -  (saved by Fritzing 0.9.9b)

parts:
  Part1 = Arduino Mega 2560 (Rev3)
  M1 = Stepper Motor - Automotive Gauge x27

nets:
  N1: Part1.D2_PWM, M1.pin_1
  N2: Part1.D3_PWM, M1.pin_2
  N3: Part1.D4_PWM, M1.pin_4
  N4: Part1.D5_PWM, M1.pin_3

notes:
  Switch middle pins (1&3 on stepper, 3&4 on arduino) in either software or on wiring.

custom parts:
  Stepper Motor - Automotive Gauge x27: Simple, Automotive Gauge stepper motor
