# Fritzing sketch ADF Wiring (saved by Fritzing 0.9.9b)

parts:
  Part1 = Arduino Mega 2560 (Rev3)
  Driver1 = 28BYJ-48 Driver Module [part_number=ULN2003 package=THT]
  SM1 = 28BYJ-48 Stepper Motor [part_number=28BYJ-48]
  Driver2 = 28BYJ-48 Driver Module [part_number=ULN2003 package=THT]
  SM2 = 28BYJ-48 Stepper Motor [part_number=28BYJ-48]
  ENCODER1 = Rotary Encoder with Knob

nets:
  N1: Part1.D12_PWM, ENCODER1.no_name_yet#5
  N2: Part1.D11_PWM, ENCODER1.no_name_yet#3
  N3: Part1.D10_PWM, ENCODER1.no_name_yet#1
  N4: Part1.D9_PWM, Driver1.IN4
  N5: Part1.D8_PWM, Driver1.IN3
  N6: Part1.D2_PWM, Driver2.IN1
  N7: Part1.D3_PWM, Driver2.IN2
  N8: Part1.D4_PWM, Driver2.IN3
  N9: Part1.D5_PWM, Driver2.IN4
  N10: Part1.D6_PWM, Driver1.IN1
  N11: Part1.D7_PWM, Driver1.IN2
  N12: Part1.5V, Driver1.Vmotor, Driver2.Vmotor
  N13: Part1.GND, ENCODER1.no_name_yet#2, ENCODER1.no_name_yet#4
  GND: Driver1.GND, Driver2.GND
  N14: Driver1.blue-pin, SM1.blue-pin
  N15: Driver1.pink-pin, SM1.pink-pin
  N16: Driver1.yellow-pin, SM1.yellow-pin
  N17: Driver1.orange-pin, SM1.orange-pin
  N18: Driver1.red-pin, SM1.red-pin
  N19: Driver2.blue-pin, SM2.blue-pin
  N20: Driver2.pink-pin, SM2.pink-pin
  N21: Driver2.yellow-pin, SM2.yellow-pin
  N22: Driver2.orange-pin, SM2.orange-pin
  N23: Driver2.red-pin, SM2.red-pin

notes:
  Needle IN1-4: D2-D5
  Gear_Ring IN1-4: D6-D9
  ADF_Encoder: D10, D11
  ADF_Push (Optional): D12

custom parts:
  28BYJ-48 Driver Module: ULN2003 Driver Module for the 28BYJ-48 Unipolar Stepper Motor LED A - Blue wire - Bottom coil left LED B - Pink wire - Top coil left LED C - Yellow wire - Bottom coil right LED D - Orange wire - Top coil right Common rail - red Connector pins: blue - pink - yellow - orange - red Control pins - IN1 to IN4 Power pins - GND & Vmotor (5-12V) On/Off jumper (if removed, power to motor is cut).
  28BYJ-48 Stepper Motor: Unipolar Stepper Motor 28BYJ-48 Top coil - pink & orange Bottom coil - blue & yellow Common rail - red Connector pins: blue - pink - yellow - orange - red
  Rotary Encoder with Knob: Rotary Encoder with 1/4" Shaft and Knob
