# Fritzing sketch Wiring Diagram -  (saved by Fritzing 1.0.1rc)

parts:
  Part1 = Arduino Mega 2560 (Rev3)
  S1 = Pushbutton [package="[THT]"]
  S2 = Pushbutton [package="[THT]"]
  S3 = Pushbutton [package="[THT]"]
  U2 = LCD-16X2 [package=lcd-16x2]  # not connected
  JP1 = Header 4 [package=screwterminal-3.5mm-4_lock]

nets:
  N1: Part1.D21/SCL, JP1.4
  N2: Part1.D20/SDA, JP1.3
  N3: Part1.GND, S1.Pin_2, S2.Pin_2, JP1.1
  N4: Part1.D2_PWM, S3.Pin_4
  N5: Part1.D3_PWM, S1.Pin_4
  N6: Part1.D4_PWM, S2.Pin_4
  N7: Part1.5V, JP1.2

notes:
  GND -> GND
  VCC -> 5V
  SDA -> SDA
  SCL -> SCL
