# Fritzing sketch Wiring Diagram -  (saved by Fritzing 0.9.9b)

parts:
  Part1 = Arduino Mega 2560 (Rev3)
  J1 = female pin header, 2 pins [form="♀ (female)"]
  J2 = female pin header, 2 pins [form="♀ (female)"]
  J3 = female pin header, 2 pins [form="♀ (female)"]
  J4 = female pin header, 2 pins [form="♀ (female)"]
  J5 = female pin header, 2 pins [form="♀ (female)"]
  J6 = female pin header, 2 pins [form="♀ (female)"]
  U1 = 7-SEGMENT-4DIGIT [package=7-segment-4digit]  # not connected
  U2 = 7-SEGMENT-4DIGIT [package=7-segment-4digit-youngsun]  # not connected
  J7 = female pin header, 2 pins [form="♀ (female)"]
  J8 = female pin header, 2 pins [form="♀ (female)"]
  J9 = female pin header, 2 pins [form="♀ (female)"]
  J10 = female pin header, 2 pins [form="♀ (female)"]  # not connected
  J11 = female pin header, 2 pins [form="♀ (female)"]  # not connected
  J12 = female pin header, 2 pins [form="♀ (female)"]  # not connected
  RE1 = Rotary Encoder [package=THT]
  RE2 = Rotary Encoder [package=THT]
  JP8 = Header 6 [package=1x06_smd_straight_alt]
  JP9 = Header 6 [package=1x06_smd_straight_alt]
  U5 = POT [package=pot_alpha_rv16af-20]
  ENCODER1 = Rotary Encoder with Knob
  S1 = Pushbutton [package="[SMD]"]
  ENCODER2 = Rotary Encoder with Knob
  U7 = POT [package=pot_alpha_rv16af-20]
  S2 = Pushbutton [package="[SMD]"]

nets:
  N1: Part1.A0, U5.S
  N2: Part1.A1, U7.S
  N3: Part1.D20/SDA, JP9.6
  N4: Part1.D19/RX1, JP9.5
  N5: Part1.D18/TX1, JP9.1
  N6: Part1.D17_PWM/RX2, RE2.EncoderPinA, JP9.2
  N7: Part1.D16_PWM/TX2, Part1.GND, Part1.D8_PWM, J1.pin2, RE1.EncoderPinB, RE2.EncoderPinB, JP8.4, JP9.4, U5.A, ENCODER1.no_name_yet#2, ENCODER1.no_name_yet#4, S1.Pin_3, S1.Pin_4, ENCODER2.no_name_yet#2, ENCODER2.no_name_yet#4, U7.A, S2.Pin_3, S2.Pin_4
  N8: Part1.D15/RX3, ENCODER2.no_name_yet#3
  N9: Part1.D14/TX3, ENCODER2.no_name_yet#1
  N10: Part1.D13_PWM, ENCODER2.no_name_yet#5
  N11: Part1.D12_PWM, JP8.6
  N12: Part1.D11_PWM, JP8.5
  N13: Part1.D10_PWM, JP8.1
  N14: Part1.D9_PWM, RE1.EncoderPinA, JP8.2
  N15: Part1.5V, J1.pin1, U5.E, U7.E
  N16: Part1.D2_PWM, J2.pin1
  N17: Part1.D3_PWM, J3.pin2
  N18: Part1.D4_PWM, J2.pin2, J3.pin1
  N19: Part1.D5_PWM, ENCODER1.no_name_yet#5
  N20: Part1.D6_PWM, ENCODER1.no_name_yet#1
  N21: Part1.D7_PWM, ENCODER1.no_name_yet#3
  N22: J4.pin1, J7.pin1
  N23: J4.pin2, J7.pin2
  N24: J5.pin1, J8.pin1
  N25: J5.pin2, J6.pin1, J8.pin2, J9.pin1
  N26: J6.pin2, J9.pin2

notes:
  VCC -> 5V
  GND -> GND
  DIN -> 2
  CS -> 3
  CLK - > 4
  COM Dual
  b -> 10
  a -> 9
  SW -> NA
  COM -> GND
  A -> 11
  B -> 12
  DO NOT MIX UP ROTARY ENCODER AND POTENTIOMETER WIRING!
  Com PWR -> 5
  Com Volume A -> 6
  Com Volume B -> 7
  Com Swap: 8
  Nav Ident -> 13
  Nav Volume A -> 14
  Nav Volume B -> 15
  Nav Swap: 16
  NAV Dual
  b -> 18
  a -> 17
  SW -> NA
  COM -> GND
  A -> 19
  B -> 20
  If using potentiometer (not encoder) A0 and A1

custom parts:
  Rotary Encoder with Knob: Rotary Encoder with 1/4" Shaft and Knob
