# Fritzing sketch Wiring Diagram -  (saved by Fritzing 1.0.7)

parts:
  Part1 = Arduino Mega 2560 (Rev3)
  LED2 = smd LED [color="Red (633nm)" package="0805 [SMD]"]
  U1 = SWITCH_SPDT [package=kps-1290]
  R1 = Resistor [tolerance=±5% power=0.25W resistance=220 package=THT]

nets:
  N1: Part1.D31, U1.O
  N2: Part1.D32, U1.S
  N3: Part1.D33, R1.Pin_1
  N4: LED2.cathode, U1.P

notes:
  GND, ON-D31, RST-D32, LED-D33
  Cutlist:
  x1 BLK 110cm
  x2 WHT 110cm
  x1 BLK 15cm
  x1 WHT 125cm
  Refer to video wiring.
